// Logisim project CPU.circ as structural Verilog: 4 circuits, main circuit CPU
module CPU (
  input  in_1,
  input  in_2,
  output [15:0] out_3
);

  wire cu_1_out_3;
  wire [3:0] cu_1_dst, cu_1_opcode, cu_1_src1, cu_1_src2;
  wire [15:0] reg_1_out1, reg_1_out2;

  CU cu_1 (
    .SUB(in_2), .DST(cu_1_dst), .SRC1(cu_1_src1), .SRC2(cu_1_src2), .OPCODE(cu_1_opcode), .in_1(in_1),
    .out_3(cu_1_out_3));
  REG reg_1 (
    .IN(out_3), .WR_ADR(cu_1_dst), .SRC1(cu_1_src1), .SRC2(cu_1_src2), .OUT1(reg_1_out1), .OUT2(reg_1_out2),
    .CL(cu_1_out_3));
  ALU alu_1 (.IN1(reg_1_out1), .IN2(reg_1_out2), .OPCODE(cu_1_opcode), .OUT(out_3));
endmodule

module ALU (
  input  [15:0] IN1,
  input  [15:0] IN2,
  input  [3:0] OPCODE,
  output [15:0] OUT
);

  wire [15:0] adder_1_out, and_1_out, divider_1_out, multiplier_1_out, nand_1_out, negator_1_out, nor_1_out,
       not_1_out, or_1_out, subtractor_1_out, xnor_1_out, xor_1_out;

  assign not_1_out = ~IN2;  // NOT_Gate not_1, 16 bits wide
  Adder #(.width(16)) adder_1 (.a(IN1), .b(IN2), .out(adder_1_out));  // open: cin, cout
  Subtractor #(.width(16)) subtractor_1 (.a(IN1), .b(IN2), .out(subtractor_1_out));  // open: bin, bout
  Multiplier #(.width(16)) multiplier_1 (.a(IN1), .b(IN2), .out(multiplier_1_out));  // open: cin, cout
  Divider #(.width(16)) divider_1 (.a(IN1), .b(IN2), .out(divider_1_out));  // open: upper, rem
  Negator #(.width(16)) negator_1 (.in(IN2), .out(negator_1_out));
  assign and_1_out = IN1 & IN2;  // AND_Gate and_1, 16 bits wide
  assign or_1_out = IN1 | IN2;  // OR_Gate or_1, 16 bits wide
  assign nand_1_out = ~(IN1 & IN2);  // NAND_Gate nand_1, 16 bits wide
  assign nor_1_out = ~(IN1 | IN2);  // NOR_Gate nor_1, 16 bits wide
  assign xor_1_out = IN1 ^ IN2;  // XOR_Gate xor_1, 16 bits wide
  assign xnor_1_out = ~(IN1 ^ IN2);  // XNOR_Gate xnor_1, 16 bits wide
  Multiplexer #(.select(4), .width(16)) multiplexer_1 (
    .in0(adder_1_out), .in1(subtractor_1_out), .in2(multiplier_1_out), .in3(divider_1_out),
    .in4(negator_1_out), .in5(and_1_out), .in6(or_1_out), .in7(not_1_out), .in8(nand_1_out), .in9(nor_1_out),
    .in10(xor_1_out), .in11(xnor_1_out), .in12({16{1'b0}}), .in13({16{1'b0}}), .in14({16{1'b0}}),
    .in15({16{1'b0}}), .out(OUT), .sel(OPCODE));  // open: en
endmodule

module REG (
  input  [15:0] IN,
  input  [3:0] WR_ADR,
  input  CL,
  input  [3:0] SRC1,
  input  [3:0] SRC2,
  output [15:0] OUT1,
  output [15:0] OUT2
);

  wire decoder_1_out0, decoder_1_out1, decoder_1_out2, decoder_1_out3, decoder_1_out4, decoder_1_out5,
       decoder_1_out6, decoder_1_out7, decoder_1_out8;
  wire [15:0] register_1_q, register_2_q, register_3_q, register_5_q, register_6_q, register_7_q,
       register_8_q;

  Decoder #(.select(4)) decoder_1 (
    .out0(decoder_1_out0), .out1(decoder_1_out1), .out2(decoder_1_out2), .out3(decoder_1_out3),
    .out4(decoder_1_out4), .out5(decoder_1_out5), .out6(decoder_1_out6), .out7(decoder_1_out7),
    .out8(decoder_1_out8), .out9(decoder_1_out8), .out10(decoder_1_out8), .out11(decoder_1_out8),
    .out12(decoder_1_out8), .out13(decoder_1_out8), .out14(decoder_1_out8), .out15(decoder_1_out8),
    .sel(WR_ADR));  // open: en
  Register #(.width(16)) register_1 (.D(IN), .en(decoder_1_out0), .Q(register_1_q), .clk(CL));  // open: clr
  Register #(.width(16)) register_2 (.D(IN), .en(decoder_1_out1), .Q(register_2_q), .clk(CL));  // open: clr
  Register #(.width(16)) register_3 (.D(IN), .en(decoder_1_out2), .Q(register_3_q), .clk(CL));  // open: clr
  Register #(.width(16)) register_4 (.D(IN), .en(decoder_1_out3), .Q(register_3_q), .clk(CL));  // open: clr
  Register #(.width(16)) register_5 (.D(IN), .en(decoder_1_out4), .Q(register_5_q), .clk(CL));  // open: clr
  Register #(.width(16)) register_6 (.D(IN), .en(decoder_1_out5), .Q(register_6_q), .clk(CL));  // open: clr
  Register #(.width(16)) register_7 (.D(IN), .en(decoder_1_out6), .Q(register_7_q), .clk(CL));  // open: clr
  Register #(.width(16)) register_8 (.D(IN), .en(decoder_1_out7), .Q(register_8_q), .clk(CL));  // open: clr
  Multiplexer #(.select(4), .width(16)) multiplexer_1 (
    .in0(register_1_q), .in1(register_2_q), .in2(register_3_q), .in3(register_3_q), .in4(register_5_q),
    .in5(register_6_q), .in6(register_7_q), .in7(register_8_q), .in8({16{1'b0}}), .in9({16{1'b0}}),
    .in10({16{1'b0}}), .in11({16{1'b0}}), .in12({16{1'b0}}), .in13({16{1'b0}}), .in14({16{1'b0}}),
    .in15({16{1'b0}}), .out(OUT1), .sel(SRC1));  // open: en
  Multiplexer #(.select(4), .width(16)) multiplexer_2 (
    .in0(register_1_q), .in1(register_2_q), .in2(register_3_q), .in3(register_3_q), .in4(register_5_q),
    .in5(register_6_q), .in6(register_7_q), .in7(register_8_q), .in8({16{1'b0}}), .in9({16{1'b0}}),
    .in10({16{1'b0}}), .in11({16{1'b0}}), .in12({16{1'b0}}), .in13({16{1'b0}}), .in14({16{1'b0}}),
    .in15({16{1'b0}}), .out(OUT2), .sel(SRC2));  // open: en
  // also tied to GND on the sheet: decoder_1_out8
endmodule

module CU (
  input  in_1,
  input  SUB,
  output out_3,
  output [3:0] DST,
  output [3:0] SRC1,
  output [3:0] SRC2,
  output [3:0] OPCODE
);

  wire [15:0] adder_1_out, multiplexer_1_out, register_1_q, subtractor_1_out;

  Register #(.width(16)) register_1 (.D(multiplexer_1_out), .Q(register_1_q), .clk(in_1));  // open: en, clr
  Adder #(.width(16)) adder_1 (.a(register_1_q), .b(16'h1), .out(adder_1_out));  // open: cin, cout
  Subtractor #(.width(16)) subtractor_1 (.a(register_1_q), .b(16'h1), .out(subtractor_1_out));  // open: bin, bout
  Multiplexer #(.width(16)) multiplexer_1 (
    .in0(adder_1_out), .in1(subtractor_1_out), .out(multiplexer_1_out), .sel(SUB));  // open: en
  ROM #(.addrWidth(16), .dataWidth(16)) rom_1 (.addr(register_1_q), .data({OPCODE, SRC2, SRC1, DST}));  // open: sel

  assign out_3 = in_1;

  // Notes on the sheet:
  //   contents of rom_1 (hex, n*v repeats v):
  //   312 1412 5562 1843 2512 5642 3564 5423 4 4123 1254 3464 7956 3467 4512 1227 6568 9780 4567 4612 6237
  //   7935 6723 456 2347 46 8 24 1235 6713 3512 35 23 78 246 5624 7 5746 1235 3467 23 2357 26 3 4 7 34 0 4
  //   3247
endmodule
